// Logisim project riscv.circ as structural Verilog: 6 circuits, main circuit main
module main (
);


  // Notes on the sheet:
  //   MAIN CIRCUIT
endmodule

module CU (
);


  // Notes on the sheet:
  //   CONTROL UNIT
endmodule

module ALU (
  input  [1:0] OPCODE,
  input  [31:0] INPUT_A,
  input  [31:0] INPUT_B
);

  wire [31:0] AND, DIFF, OR, RES, SUM;

  Adder #(.width(32)) adder_1 (.a(INPUT_A), .b(INPUT_B), .out(SUM), .cin(1'b0));  // open: cout
  assign OR = INPUT_A | INPUT_B;  // OR_Gate or_1, 32 bits wide
  Subtractor #(.width(32)) subtractor_1 (.a(INPUT_A), .b(INPUT_B), .out(DIFF), .bin(1'b0));  // open: bout
  assign AND = INPUT_A & INPUT_B;  // AND_Gate and_1, 32 bits wide
  Multiplexer #(.select(2), .width(32), .enable("false")) multiplexer_1 (
    .in0(AND), .in1(OR), .in2(SUM), .in3(DIFF), .out(RES), .sel(OPCODE));

  // Other names for the same wires on the sheet: IN_A[31:0] = INPUT_A; IN_B[31:0] = INPUT_B

  // Notes on the sheet:
  //   ARITHMETIC OPERATIONS
  //   LOGICAL OPERATIONS
  //   ARITHMETIC AND LOGIC UNIT
  //   OPERATION DECODER
endmodule

module RF (
  input  ENABLE_WRITE,
  input  [31:0] DATA_IN,
  input  CLOCK,
  input  CLEAR,
  input  [31:0] RA_OUT,
  input  [2:0] SELECT_RA,
  input  [2:0] SELECT_RB,
  input  [2:0] SELECT_RO,
  input  [31:0] RB_OUT
);

  wire EN_R1, EN_R2, EN_R3, EN_R4, EN_R5, EN_R6, EN_R7, EN_R8;
  wire [31:0] R1_OUT, R2_OUT, R3_OUT, R4_OUT, R5_OUT, R6_OUT, R7_OUT, R8_OUT;

  CU cu_1 ();
  Register #(.width(32)) register_1 (.D(DATA_IN), .en(EN_R1), .Q(R1_OUT), .clk(CLOCK), .clr(CLEAR));
  Register #(.width(32)) register_2 (.D(DATA_IN), .en(EN_R3), .Q(R3_OUT), .clk(CLOCK), .clr(CLEAR));
  Register #(.width(32)) register_3 (.D(DATA_IN), .en(EN_R5), .Q(R5_OUT), .clk(CLOCK), .clr(CLEAR));
  // Probe on R1_OUT
  // Probe on R2_OUT
  // Probe on R3_OUT
  // Probe on R4_OUT
  // Probe on R5_OUT
  // Probe on R6_OUT
  // Probe on R7_OUT
  // Probe on R8_OUT
  Register #(.width(32)) register_4 (.D(DATA_IN), .en(EN_R2), .Q(R2_OUT), .clk(CLOCK), .clr(CLEAR));
  Register #(.width(32)) register_5 (.D(DATA_IN), .en(EN_R4), .Q(R4_OUT), .clk(CLOCK), .clr(CLEAR));
  Register #(.width(32)) register_6 (.D(DATA_IN), .en(EN_R6), .Q(R6_OUT), .clk(CLOCK), .clr(CLEAR));
  Register #(.width(32)) register_7 (.D(DATA_IN), .en(EN_R7), .Q(R7_OUT), .clk(CLOCK), .clr(CLEAR));
  Register #(.width(32)) register_8 (.D(DATA_IN), .en(EN_R8), .Q(R8_OUT), .clk(CLOCK), .clr(CLEAR));
  Multiplexer #(.select(3), .width(32), .enable("false")) multiplexer_1 (
    .in0(R1_OUT), .in1(R2_OUT), .in2(R3_OUT), .in3(R4_OUT), .in4(R5_OUT), .in5(R6_OUT), .in6(R7_OUT),
    .in7(R8_OUT), .out(RA_OUT), .sel(SELECT_RA));
  Demultiplexer #(.select(3), .enable("false")) demultiplexer_1 (
    .out0(EN_R1), .out1(EN_R2), .out2(EN_R3), .out3(EN_R4), .out4(EN_R5), .out5(EN_R6), .out6(EN_R7),
    .out7(EN_R8), .in(ENABLE_WRITE), .sel(SELECT_RO));
  Multiplexer #(.select(3), .width(32), .enable("false")) multiplexer_2 (
    .in0(R1_OUT), .in1(R2_OUT), .in2(R3_OUT), .in3(R4_OUT), .in4(R5_OUT), .in5(R6_OUT), .in6(R7_OUT),
    .in7(R8_OUT), .out(RB_OUT), .sel(SELECT_RB));

  // Other names for the same wires on the sheet: CLK = CLOCK; CLR = CLEAR; EN_WRITE = ENABLE_WRITE; RA[31:0] = RA_OUT;
  //   RB[31:0] = RB_OUT; RIN[31:0] = DATA_IN; SEL_RA[2:0] = SELECT_RA; SEL_RB[2:0] = SELECT_RB;
  //   SEL_RO[2:0] = SELECT_RO

  // Notes on the sheet:
  //   REGISTER FILE
  //   REGISTER PROBES
  //   RA SELECT
  //   WRITE SELECT
  //   RB SELECT
endmodule

module MU (
  input  [15:0] IN_ADDRESS,
  input  [31:0] OUT_DATA,
  input  [31:0] IN_DATA,
  input  WRITE_ENABLE,
  input  CLEAR,
  input  CLOCK,
  input  READ_ENABLE
);

  RAM #(.addrWidth(16), .dataWidth(32), .bus("separate")) ram_1 (
    .addr(IN_ADDRESS), .din(IN_DATA), .data(OUT_DATA), .str(WRITE_ENABLE), .sel(1'b1), .clk(CLOCK),
    .ld(READ_ENABLE), .clr(CLEAR));

  // Notes on the sheet:
  //   MEMORY UNIT
endmodule

module IAG (
);


  // Notes on the sheet:
  //   INSTRUCTION ADDRESS GENERATOR
endmodule
